// Logisim project project.circ as structural Verilog: 10 circuits, main circuit PC
module main (
  input  in_1,
  output [15:0] showing_PC
);

  wire beq, bgt, bne, clock_1_out, control_unit_1_r_type, is_beq, is_bgt, is_jr, is_jump, jr, lw, r_w_1_r_w,
       sw;
  wire [2:0] alu_control_1_select;
  wire [4:0] control_unit_1_alu_op, control_unit_1_op_code, control_unit_1_part_2_2, control_unit_1_part_3_2,
       control_unit_1_part_4_2, control_unit_1_part_5_2, input_output_1_input_1, input_output_1_input_2,
       input_output_1_output;
  wire [15:0] B_Address, J__Address, J_Address, jr_Address, register_1_q;
  wire [24:0] ram_1_data;
  wire [31:0] alu_1_output, input_output_1_input_to_alu_1, input_output_1_input_to_alu_2, multiplexer_1_out,
       ram_2_data, register_2_data_1, register_2_data_2;

  Clock clock_1 (.out(clock_1_out));
  PC pc_1 (
    .inputt(register_1_q), .beq(beq), .bne(bne), .bgt(bgt), .jr(jr), .is_Jump(is_jump), .is_jr(is_jr),
    .is_bgt(is_bgt), .is_bne(is_bgt), .is_beq(is_beq), .jr_address(jr_Address), .B_address(B_Address),
    .j_address(J__Address), .answer(showing_PC));
  Register #(.width(16)) register_1 (.D(showing_PC), .Q(register_1_q), .clk(clock_1_out), .clr(in_1));  // open: en
  RAM #(.addrWidth(16), .dataWidth(25)) ram_1 (.addr(register_1_q), .data(ram_1_data));  // open: sel, clk, ld, clr
  control_unit control_unit_1 (
    .part_1(ram_1_data[24:20]), .part_2(ram_1_data[19:15]), .part_4(ram_1_data[9:5]),
    .part_3(ram_1_data[14:10]), .part_5(ram_1_data[4:0]), .Jump(is_jump), .ALU_op(control_unit_1_alu_op),
    .part_5_2(control_unit_1_part_5_2), .part_4_2(control_unit_1_part_4_2),
    .part_3_2(control_unit_1_part_3_2), .part_2_2(control_unit_1_part_2_2), .R_Type(control_unit_1_r_type),
    .op_code(control_unit_1_op_code), .LW(lw), .SW(sw), .BEQ(is_beq), .BNE(is_bgt), .JR(is_jr), .BGT(is_bgt),
    .branch_address(B_Address), .J_address(J_Address), .Branch(control_unit_1_r_type));
  R_W r_w_1 (.SW_prime(sw), .beq(is_beq), .bne(is_bgt), .bqt(is_bgt), .jr(is_jr), .R_W(r_w_1_r_w));
  ALU_control alu_control_1 (
    .op_code(control_unit_1_op_code), .ALU_op(control_unit_1_alu_op), .select(alu_control_1_select));
  Input___Output input_output_1 (
    .P_5(control_unit_1_part_5_2), .P_4(control_unit_1_part_4_2), .P_3(control_unit_1_part_3_2),
    .P_2(control_unit_1_part_2_2), .R_type(control_unit_1_r_type), .Data_2(register_2_data_2),
    .Data_1(register_2_data_1), .input_1(input_output_1_input_1), .input_2(input_output_1_input_2),
    .\output (input_output_1_output), .input_to_ALU_1(input_output_1_input_to_alu_1),
    .input_to_ALU_2(input_output_1_input_to_alu_2), .Branch(control_unit_1_r_type));
  ALU alu_1 (
    .\output (alu_1_output), .input_1(input_output_1_input_to_alu_1),
    .input_2(input_output_1_input_to_alu_2), .selector(alu_control_1_select), .BGT(bgt), .beq(beq), .bne(bne));
  register register_2 (
    .input_1(input_output_1_input_1), .input_2(input_output_1_input_2), .\output (input_output_1_output),
    .Data_1(register_2_data_1), .Data_2(register_2_data_2), .Data_in(multiplexer_1_out), .CLEAR(in_1),
    .R_W(r_w_1_r_w), .Clock(clock_1_out));
  Multiplexer #(.width(32), .enable("false")) multiplexer_1 (
    .in0(alu_1_output), .in1(ram_2_data), .out(multiplexer_1_out), .sel(lw));
  RAM #(.addrWidth(16), .dataWidth(32), .bus("separate")) ram_2 (
    .addr(alu_1_output[15:0]), .din(input_output_1_input_to_alu_2), .data(ram_2_data), .str(sw),
    .clk(clock_1_out), .ld(lw));  // open: sel, clr

  // Other names for the same wires on the sheet: is_bne = is_bgt
endmodule

module PC (
  input  jr,
  input  beq,
  input  bne,
  input  bgt,
  input  [15:0] j_address,
  input  [15:0] jr_address,
  input  [15:0] B_address,
  input  [15:0] inputt,
  output is_jr,
  output is_beq,
  output is_bne,
  output is_bgt,
  output is_Jump,
  output [15:0] answer
);

  wire and_1_out, and_2_out, and_3_out, and_4_out, not_1_out, or_1_out, or_2_out;
  wire [15:0] adder_1_out, adder_2_out, multiplexer_1_out, multiplexer_2_out, multiplexer_3_out;

  Adder #(.width(16)) adder_1 (.a(B_address), .b(inputt), .out(adder_1_out));  // open: cin, cout
  Multiplexer #(.width(16), .enable("false")) multiplexer_1 (
    .in0({16{1'b0}}), .in1(j_address), .out(multiplexer_1_out), .sel(is_Jump));
  Adder #(.width(16)) adder_2 (.a(inputt), .b(16'h1), .out(adder_2_out));  // open: cin, cout
  and and_1 (and_1_out, is_jr, jr);
  Multiplexer #(.width(16), .enable("false")) multiplexer_2 (
    .in0(multiplexer_1_out), .in1(jr_address), .out(multiplexer_2_out), .sel(and_1_out));
  and and_2 (and_2_out, is_beq, beq);
  and and_3 (and_3_out, is_bne, bne);
  or or_1 (or_1_out, and_2_out, and_3_out, and_4_out);
  and and_4 (and_4_out, is_bgt, bgt);
  Multiplexer #(.width(16), .enable("false")) multiplexer_3 (
    .in0(multiplexer_2_out), .in1(adder_1_out), .out(multiplexer_3_out), .sel(or_1_out));
  or or_2 (or_2_out, is_Jump, and_1_out, or_1_out);
  not not_1 (not_1_out, or_2_out);
  Multiplexer #(.width(16), .enable("false")) multiplexer_4 (
    .in0(multiplexer_3_out), .in1(adder_2_out), .out(answer), .sel(not_1_out));
endmodule

// Control Unit
module control_unit (
  input  [4:0] part_5,
  input  [4:0] part_4,
  input  [4:0] part_3,
  input  [4:0] part_2,
  input  [4:0] part_1,
  output [15:0] branch_address,
  output [4:0] op_code,
  output [4:0] ALU_op,
  output [4:0] part_5_2,
  output [4:0] part_4_2,
  output [4:0] part_3_2,
  output [4:0] part_2_2,
  output R_Type,
  output BGT,
  output LW,
  output SW,
  output BEQ,
  output BNE,
  output JR,
  output Jump,
  output Branch,
  output [15:0] J_address
);

  assign branch_address = {{6{1'b0}}, {part_4, part_5}};  // Bit_Extender bit_extender_1
  assign J_address = {{1{1'b0}}, {part_3, part_4, part_5}};  // Bit_Extender bit_extender_2
  op_code_explane op_code_explane_1 (
    .part_1(part_1), .bgt(BGT), .lw(LW), .sw(SW), .beq(BEQ), .bne(BNE), .jr(JR), .j(Jump), .R_Type(R_Type),
    .ALU_op(ALU_op));  // open: slt
  or or_1 (Branch, BNE, BEQ, BGT);

  assign op_code = part_1;
  assign part_2_2 = part_2;
  assign part_3_2 = part_3;
  assign part_4_2 = part_4;
  assign part_5_2 = part_5;
endmodule

module ALU_control (
  input  [4:0] op_code,
  input  [4:0] ALU_op,
  output [2:0] select
);

  wire [2:0] multiplexer_2_out, multiplexer_3_out, multiplexer_4_out, multiplexer_5_out;

  Multiplexer #(.width(3), .enable("false")) multiplexer_1 (
    .in0(multiplexer_5_out), .in1(op_code[2:0]), .out(select), .sel(ALU_op[0]));
  Multiplexer #(.width(3), .enable("false")) multiplexer_2 (
    .in0(3'b000), .in1(3'b000), .out(multiplexer_2_out), .sel(ALU_op[1]));
  Multiplexer #(.width(3), .enable("false")) multiplexer_3 (
    .in0(multiplexer_2_out), .in1(3'b100), .out(multiplexer_3_out), .sel(ALU_op[2]));
  Multiplexer #(.width(3), .enable("false")) multiplexer_4 (
    .in0(multiplexer_3_out), .in1(3'b111), .out(multiplexer_4_out), .sel(ALU_op[3]));
  Multiplexer #(.width(3), .enable("false")) multiplexer_5 (
    .in0(multiplexer_4_out), .in1(3'b100), .out(multiplexer_5_out), .sel(ALU_op[4]));

  // Notes on the sheet:
  //   1 : math 
  //   2 : bgt / slt
  //   ALU Control
  //   3 : lw / sw
  //   4 : beq / bne
  //   5 : jr
endmodule

// Register
module register (
  input  [31:0] Data_in,
  input  CLEAR,
  input  Clock,
  input  R_W,
  input  [4:0] input_1,
  input  [4:0] \output ,
  input  [4:0] input_2,
  output [31:0] Data_1,
  output [31:0] Data_2
);

  wire and_1_out, and_2_out, and_3_out, and_4_out, and_5_out, and_6_out, and_7_out, and_8_out, and_9_out,
       and_10_out, and_11_out, and_12_out, and_13_out, and_14_out, and_15_out, and_16_out, and_17_out,
       and_18_out, and_19_out, and_20_out, and_21_out, and_22_out, and_23_out, and_24_out, and_25_out,
       and_26_out, and_27_out, and_28_out, and_29_out, and_30_out, and_31_out, and_32_out, multiplexer_1_out,
       Reg_in_0, Reg_in_1, Reg_in_2, Reg_in_3, Reg_in_4, Reg_in_5, Reg_in_6, Reg_in_7, Reg_in_8, Reg_in_9,
       Reg_in_10, Reg_in_11, Reg_in_12, Reg_in_13, Reg_in_14, Reg_in_15, Reg_in_16, Reg_in_17, Reg_in_18,
       Reg_in_19, Reg_in_20, Reg_in_21, Reg_in_22, Reg_in_23, Reg_in_24, Reg_in_25, Reg_in_26, Reg_in_27,
       Reg_in_28, Reg_in_29, Reg_in_30, Reg_in_31;
  wire [31:0] Reg_out_0, Reg_out_1, Reg_out_2, Reg_out_3, Reg_out_4, Reg_out_5, Reg_out_6, Reg_out_7,
       Reg_out_8, Reg_out_9, Reg_out_10, Reg_out_11, Reg_out_12, Reg_out_13, Reg_out_14, Reg_out_15,
       Reg_out_16, Reg_out_17, Reg_out_18, Reg_out_19, Reg_out_20, Reg_out_21, Reg_out_22, Reg_out_23,
       Reg_out_24, Reg_out_25, Reg_out_26, Reg_out_27, Reg_out_28, Reg_out_29, Reg_out_30, Reg_out_31,
       register_1_q;

  Multiplexer #(.select(5), .enable("false")) multiplexer_1 (
    .in0(Reg_in_0), .in1(Reg_in_1), .in2(Reg_in_2), .in3(Reg_in_3), .in4(Reg_in_4), .in5(Reg_in_5),
    .in6(Reg_in_6), .in7(Reg_in_7), .in8(Reg_in_8), .in9(Reg_in_9), .in10(Reg_in_10), .in11(Reg_in_11),
    .in12(Reg_in_12), .in13(Reg_in_13), .in14(Reg_in_14), .in15(Reg_in_15), .in16(Reg_in_16),
    .in17(Reg_in_17), .in18(Reg_in_18), .in19(Reg_in_19), .in20(Reg_in_20), .in21(Reg_in_21),
    .in22(Reg_in_22), .in23(Reg_in_23), .in24(Reg_in_24), .in25(Reg_in_25), .in26(Reg_in_26),
    .in27(Reg_in_27), .in28(Reg_in_28), .in29(Reg_in_29), .in30(Reg_in_30), .in31(Reg_in_31),
    .out(multiplexer_1_out), .sel(\output ));
  Register #(.width(32)) register_1 (.D(Data_in), .Q(register_1_q), .clk(Clock), .clr(CLEAR));  // open: en
  and and_1 (and_1_out, Reg_in_0, R_W);
  and and_2 (and_2_out, Reg_in_1, R_W);
  and and_3 (and_3_out, Reg_in_2, R_W);
  and and_4 (and_4_out, Reg_in_3, R_W);
  and and_5 (and_5_out, Reg_in_4, R_W);
  and and_6 (and_6_out, Reg_in_5, R_W);
  and and_7 (and_7_out, Reg_in_6, R_W);
  and and_8 (and_8_out, Reg_in_7, R_W);
  and and_9 (and_9_out, Reg_in_8, R_W);
  and and_10 (and_10_out, Reg_in_9, R_W);
  and and_11 (and_11_out, Reg_in_10, R_W);
  and and_12 (and_12_out, Reg_in_11, R_W);
  and and_13 (and_13_out, Reg_in_12, R_W);
  and and_14 (and_14_out, Reg_in_13, R_W);
  and and_15 (and_15_out, Reg_in_14, R_W);
  and and_16 (and_16_out, Reg_in_15, R_W);
  and and_17 (and_17_out, Reg_in_16, R_W);
  and and_18 (and_18_out, Reg_in_17, R_W);
  and and_19 (and_19_out, Reg_in_18, R_W);
  and and_20 (and_20_out, Reg_in_19, R_W);
  and and_21 (and_21_out, Reg_in_20, R_W);
  and and_22 (and_22_out, Reg_in_21, R_W);
  and and_23 (and_23_out, Reg_in_22, R_W);
  and and_24 (and_24_out, Reg_in_23, R_W);
  and and_25 (and_25_out, Reg_in_24, R_W);
  and and_26 (and_26_out, Reg_in_25, R_W);
  and and_27 (and_27_out, Reg_in_26, R_W);
  and and_28 (and_28_out, Reg_in_27, R_W);
  and and_29 (and_29_out, Reg_in_28, R_W);
  and and_30 (and_30_out, Reg_in_29, R_W);
  and and_31 (and_31_out, Reg_in_30, R_W);
  and and_32 (and_32_out, Reg_in_31, R_W);
  Register #(.width(32)) Register_0 (.D(register_1_q), .Q(Reg_out_0), .clk(and_1_out), .clr(CLEAR));  // open: en
  Register #(.width(32)) Register_1_dup2 (.D(register_1_q), .Q(Reg_out_1), .clk(and_2_out), .clr(CLEAR));  // open: en
  Register #(.width(32)) Register_3 (.D(register_1_q), .Q(Reg_out_2), .clk(and_3_out), .clr(CLEAR));  // open: en
  Register #(.width(32)) Register_4 (.D(register_1_q), .Q(Reg_out_3), .clk(and_4_out), .clr(CLEAR));  // open: en
  Register #(.width(32)) Register_4_2 (.D(register_1_q), .Q(Reg_out_4), .clk(and_5_out), .clr(CLEAR));  // open: en
  Register #(.width(32)) Register_5 (.D(register_1_q), .Q(Reg_out_5), .clk(and_6_out), .clr(CLEAR));  // open: en
  Register #(.width(32)) Register_6 (.D(register_1_q), .Q(Reg_out_6), .clk(and_7_out), .clr(CLEAR));  // open: en
  Register #(.width(32)) Register_7 (.D(register_1_q), .Q(Reg_out_7), .clk(and_8_out), .clr(CLEAR));  // open: en
  Register #(.width(32)) Register_9 (.D(register_1_q), .Q(Reg_out_8), .clk(and_9_out), .clr(CLEAR));  // open: en
  Register #(.width(32)) Register_10 (.D(register_1_q), .Q(Reg_out_9), .clk(and_10_out), .clr(CLEAR));  // open: en
  Register #(.width(32)) Register_10_2 (.D(register_1_q), .Q(Reg_out_10), .clk(and_11_out), .clr(CLEAR));  // open: en
  Register #(.width(32)) Register_11 (.D(register_1_q), .Q(Reg_out_11), .clk(and_12_out), .clr(CLEAR));  // open: en
  Register #(.width(32)) Register_12 (.D(register_1_q), .Q(Reg_out_12), .clk(and_13_out), .clr(CLEAR));  // open: en
  Register #(.width(32)) Register_13 (.D(register_1_q), .Q(Reg_out_13), .clk(and_14_out), .clr(CLEAR));  // open: en
  Register #(.width(32)) Register_15 (.D(register_1_q), .Q(Reg_out_14), .clk(and_15_out), .clr(CLEAR));  // open: en
  Register #(.width(32)) Register_15_2 (.D(register_1_q), .Q(Reg_out_15), .clk(and_16_out), .clr(CLEAR));  // open: en
  Register #(.width(32)) Register_16 (.D(register_1_q), .Q(Reg_out_16), .clk(and_17_out), .clr(CLEAR));  // open: en
  Register #(.width(32)) Register_17 (.D(register_1_q), .Q(Reg_out_17), .clk(and_18_out), .clr(CLEAR));  // open: en
  Register #(.width(32)) Register_18 (.D(register_1_q), .Q(Reg_out_18), .clk(and_19_out), .clr(CLEAR));  // open: en
  Register #(.width(32)) Register_19 (.D(register_1_q), .Q(Reg_out_19), .clk(and_20_out), .clr(CLEAR));  // open: en
  Register #(.width(32)) Register_20 (.D(register_1_q), .Q(Reg_out_20), .clk(and_21_out), .clr(CLEAR));  // open: en
  Register #(.width(32)) Register_21 (.D(register_1_q), .Q(Reg_out_21), .clk(and_22_out), .clr(CLEAR));  // open: en
  Register #(.width(32)) Register_22 (.D(register_1_q), .Q(Reg_out_22), .clk(and_23_out), .clr(CLEAR));  // open: en
  Register #(.width(32)) Register_23 (.D(register_1_q), .Q(Reg_out_23), .clk(and_24_out), .clr(CLEAR));  // open: en
  Register #(.width(32)) Register_24 (.D(register_1_q), .Q(Reg_out_24), .clk(and_25_out), .clr(CLEAR));  // open: en
  Register #(.width(32)) Register_25 (.D(register_1_q), .Q(Reg_out_25), .clk(and_26_out), .clr(CLEAR));  // open: en
  Register #(.width(32)) Register_26 (.D(register_1_q), .Q(Reg_out_26), .clk(and_27_out), .clr(CLEAR));  // open: en
  Register #(.width(32)) Register_27 (.D(register_1_q), .Q(Reg_out_27), .clk(and_28_out), .clr(CLEAR));  // open: en
  Register #(.width(32)) Register_28 (.D(register_1_q), .Q(Reg_out_28), .clk(and_29_out), .clr(CLEAR));  // open: en
  Register #(.width(32)) Register_29 (.D(register_1_q), .Q(Reg_out_29), .clk(and_30_out), .clr(CLEAR));  // open: en
  Register #(.width(32)) Register_30 (.D(register_1_q), .Q(Reg_out_30), .clk(and_31_out), .clr(CLEAR));  // open: en
  Register #(.width(32)) Register_31 (.D(register_1_q), .Q(Reg_out_31), .clk(and_32_out), .clr(CLEAR));  // open: en
  Multiplexer #(.select(5), .width(32), .enable("false")) multiplexer_2 (
    .in0(Reg_out_0), .in1(Reg_out_1), .in2(Reg_out_2), .in3(Reg_out_3), .in4(Reg_out_4), .in5(Reg_out_5),
    .in6(Reg_out_6), .in7(Reg_out_7), .in8(Reg_out_8), .in9(Reg_out_9), .in10(Reg_out_10), .in11(Reg_out_11),
    .in12(Reg_out_12), .in13(Reg_out_13), .in14(Reg_out_14), .in15(Reg_out_15), .in16(Reg_out_16),
    .in17(Reg_out_17), .in18(Reg_out_18), .in19(Reg_out_19), .in20(Reg_out_20), .in21(Reg_out_21),
    .in22(Reg_out_22), .in23(Reg_out_23), .in24(Reg_out_24), .in25(Reg_out_25), .in26(Reg_out_26),
    .in27(Reg_out_27), .in28(Reg_out_28), .in29(Reg_out_29), .in30(Reg_out_30), .in31(Reg_out_31),
    .out(Data_1), .sel(input_1));
  Multiplexer #(.select(5), .width(32), .enable("false")) multiplexer_3 (
    .in0(Reg_out_0), .in1(Reg_out_1), .in2(Reg_out_2), .in3(Reg_out_3), .in4(Reg_out_4), .in5(Reg_out_5),
    .in6(Reg_out_6), .in7(Reg_out_7), .in8(Reg_out_8), .in9(Reg_out_9), .in10(Reg_out_10), .in11(Reg_out_11),
    .in12(Reg_out_12), .in13(Reg_out_13), .in14(Reg_out_14), .in15(Reg_out_15), .in16(Reg_out_16),
    .in17(Reg_out_17), .in18(Reg_out_18), .in19(Reg_out_19), .in20(Reg_out_20), .in21(Reg_out_21),
    .in22(Reg_out_22), .in23(Reg_out_23), .in24(Reg_out_24), .in25(Reg_out_25), .in26(Reg_out_26),
    .in27(Reg_out_27), .in28(Reg_out_28), .in29(Reg_out_29), .in30(Reg_out_30), .in31(Reg_out_31),
    .out(Data_2), .sel(input_2));
  // also tied to VCC on the sheet: multiplexer_1_out

  // Notes on the sheet:
  //   W : 1
  //   R : 0
endmodule

module ALU (
  input  [31:0] input_1,
  input  [31:0] input_2,
  input  [2:0] selector,
  output BGT,
  output [31:0] \output ,
  output beq,
  output bne
);

  wire [31:0] adder_1_out, and_1_out, bit_extender_1_out, divider_1_out, multiplier_1_out, or_1_out,
       subtractor_1_out, xor_1_out;

  greater_than greater_than_1 (.input_1(input_2), .input_2(input_1), .\output (BGT));
  assign and_1_out = input_2 & input_1;  // AND_Gate and_1, 32 bits wide
  assign or_1_out = input_2 | input_1;  // OR_Gate or_1, 32 bits wide
  assign xor_1_out = input_2 ^ input_1;  // XOR_Gate xor_1, 32 bits wide
  Adder #(.width(32)) adder_1 (.a(input_2), .b(input_1), .out(adder_1_out));  // open: cin, cout
  Subtractor #(.width(32)) subtractor_1 (.a(input_2), .b(input_1), .out(subtractor_1_out));  // open: bin, bout
  Multiplier #(.width(32)) multiplier_1 (.a(input_2), .b(input_1), .out(multiplier_1_out));  // open: cin, cout
  Divider #(.width(32)) divider_1 (.a(input_2), .b(input_1), .out(divider_1_out));  // open: upper, rem
  assign bit_extender_1_out = {{31{1'b0}}, BGT};  // Bit_Extender bit_extender_1
  and and_2 (beq, ~\output [0], ~\output [1], ~\output [2], ~\output [3], ~\output [4], ~\output [5], ~\output [6], ~\output [7], ~\output [8], ~\output [9], ~\output [10], ~\output [11], ~\output [12], ~\output [13], ~\output [14], ~\output [15], ~\output [16], ~\output [17], ~\output [18], ~\output [19], ~\output [20], ~\output [21], ~\output [22], ~\output [23], ~\output [24], ~\output [25], ~\output [26], ~\output [27], ~\output [28], ~\output [29], ~\output [30], ~\output [31]);  // AND_Gate
  not not_1 (bne, beq);
  Multiplexer #(.select(3), .width(32), .enable("false")) multiplexer_1 (
    .in0(bit_extender_1_out), .in1(and_1_out), .in2(or_1_out), .in3(xor_1_out), .in4(adder_1_out),
    .in5(subtractor_1_out), .in6(multiplier_1_out), .in7(divider_1_out), .out(\output ), .sel(selector));

  // Other names for the same wires on the sheet: beq___bne[31:0] = \output 

  // Notes on the sheet:
  //   ALU
endmodule

// OP Code explane
module op_code_explane (
  input  [4:0] part_1,
  output R_Type,
  output [4:0] ALU_op,
  output bgt,
  output slt,
  output lw,
  output sw,
  output beq,
  output bne,
  output jr,
  output j
);

  wire ADD_2_out, add_out, addi_out, AND_2_out, and_out, andi_out, div2_out, DIV_2_out, div_out, MULT_2_out,
       mult_out, multi_out, not_1_out, not_2_out, not_3_out, not_4_out, not_5_out, not_6_out, not_7_out,
       not_8_out, not_9_out, not_10_out, not_11_out, not_12_out, not_13_out, not_14_out, not_15_out,
       not_16_out, not_17_out, not_18_out, not_19_out, not_20_out, not_21_out, not_22_out, not_23_out,
       not_24_out, not_25_out, not_26_out, not_27_out, not_28_out, not_29_out, not_30_out, not_31_out,
       not_32_out, not_33_out, not_34_out, not_35_out, not_36_out, not_37_out, not_38_out, not_39_out,
       not_40_out, not_41_out, not_42_out, not_43_out, not_44_out, not_45_out, not_46_out, not_47_out,
       not_48_out, not_49_out, not_50_out, not_51_out, not_52_out, not_53_out, not_54_out, not_55_out,
       not_56_out, not_57_out, OR_3_out, or_out, ori_out, SUB_2_out, sub_out, subi_out, xor_out;

  not not_1 (not_1_out, part_1[0]);
  not not_2 (not_2_out, part_1[1]);
  not not_3 (not_3_out, part_1[3]);
  not not_4 (not_4_out, part_1[4]);
  not not_5 (not_5_out, part_1[0]);
  not not_6 (not_6_out, part_1[1]);
  not not_7 (not_7_out, part_1[4]);
  not not_8 (not_8_out, part_1[1]);
  not not_9 (not_9_out, part_1[3]);
  not not_10 (not_10_out, part_1[4]);
  not not_11 (not_11_out, part_1[1]);
  not not_12 (not_12_out, part_1[4]);
  not not_13 (not_13_out, part_1[0]);
  not not_14 (not_14_out, part_1[3]);
  not not_15 (not_15_out, part_1[4]);
  not not_16 (not_16_out, part_1[0]);
  not not_17 (not_17_out, part_1[4]);
  not not_18 (not_18_out, part_1[3]);
  not not_19 (not_19_out, part_1[4]);
  not not_20 (not_20_out, part_1[4]);
  not not_21 (not_21_out, part_1[1]);
  not not_22 (not_22_out, part_1[2]);
  not not_23 (not_23_out, part_1[3]);
  not not_24 (not_24_out, part_1[4]);
  not not_25 (not_25_out, part_1[1]);
  not not_26 (not_26_out, part_1[2]);
  not not_27 (not_27_out, part_1[4]);
  not not_28 (not_28_out, part_1[0]);
  not not_29 (not_29_out, part_1[2]);
  not not_30 (not_30_out, part_1[3]);
  not not_31 (not_31_out, part_1[4]);
  not not_32 (not_32_out, part_1[0]);
  not not_33 (not_33_out, part_1[2]);
  not not_34 (not_34_out, part_1[4]);
  not not_35 (not_35_out, part_1[2]);
  not not_36 (not_36_out, part_1[3]);
  not not_37 (not_37_out, part_1[4]);
  not not_38 (not_38_out, part_1[0]);
  not not_39 (not_39_out, part_1[1]);
  not not_40 (not_40_out, part_1[2]);
  not not_41 (not_41_out, part_1[3]);
  not not_42 (not_42_out, part_1[1]);
  not not_43 (not_43_out, part_1[2]);
  not not_44 (not_44_out, part_1[3]);
  not not_45 (not_45_out, part_1[0]);
  not not_46 (not_46_out, part_1[2]);
  not not_47 (not_47_out, part_1[3]);
  not not_48 (not_48_out, part_1[2]);
  not not_49 (not_49_out, part_1[3]);
  not not_50 (not_50_out, part_1[0]);
  not not_51 (not_51_out, part_1[1]);
  not not_52 (not_52_out, part_1[3]);
  not not_53 (not_53_out, part_1[1]);
  not not_54 (not_54_out, part_1[3]);
  not not_55 (not_55_out, part_1[0]);
  not not_56 (not_56_out, part_1[3]);
  not not_57 (not_57_out, part_1[3]);
  and add (add_out, not_1_out, not_2_out, part_1[2], not_3_out, not_4_out);
  and addi (addi_out, not_5_out, not_6_out, part_1[2], part_1[3], not_7_out);
  and sub (sub_out, part_1[0], not_8_out, part_1[2], not_9_out, not_10_out);
  and subi (subi_out, part_1[0], not_11_out, part_1[2], part_1[3], not_12_out);
  and mult (mult_out, not_13_out, part_1[1], part_1[2], not_14_out, not_15_out);
  and multi (multi_out, not_16_out, part_1[1], part_1[2], part_1[3], not_17_out);
  and div (div_out, part_1[0], part_1[1], part_1[2], not_18_out, not_19_out);
  and div2 (div2_out, part_1[0], part_1[1], part_1[2], part_1[3], not_20_out);
  and \and  (and_out, part_1[0], not_21_out, not_22_out, not_23_out, not_24_out);
  and andi (andi_out, part_1[0], not_25_out, not_26_out, part_1[3], not_27_out);
  and \or  (or_out, not_28_out, part_1[1], not_29_out, not_30_out, not_31_out);
  and ori (ori_out, not_32_out, part_1[1], not_33_out, part_1[3], not_34_out);
  and \xor  (xor_out, part_1[0], part_1[1], not_35_out, not_36_out, not_37_out);
  and u_bgt (bgt, not_38_out, not_39_out, not_40_out, not_41_out, part_1[4]);
  and u_slt (ALU_op[1], part_1[0], not_42_out, not_43_out, not_44_out, part_1[4]);
  and u_lw (lw, not_45_out, part_1[1], not_46_out, not_47_out, part_1[4]);
  and u_sw (sw, part_1[0], part_1[1], not_48_out, not_49_out, part_1[4]);
  and u_beq (beq, not_50_out, not_51_out, part_1[2], not_52_out, part_1[4]);
  and u_bne (bne, part_1[0], not_53_out, part_1[2], not_54_out, part_1[4]);
  and u_jr (ALU_op[4], not_55_out, part_1[1], part_1[2], not_56_out, part_1[4]);
  and u_j (j, part_1[0], part_1[1], part_1[2], not_57_out, part_1[4]);
  or or_2 (R_Type, add_out, sub_out, mult_out, div_out, and_out, or_out, xor_out);
  or ADD_2 (ADD_2_out, add_out, addi_out);
  or SUB_2 (SUB_2_out, sub_out, subi_out);
  or MULT_2 (MULT_2_out, mult_out, multi_out);
  or DIV_2 (DIV_2_out, div_out, div2_out);
  or AND_2 (AND_2_out, and_out, andi_out);
  or OR_3 (OR_3_out, or_out, ori_out);
  or or_4 (ALU_op[2], lw, sw);
  or or_5 (ALU_op[3], beq, bne);
  or or_6 (ALU_op[0], ADD_2_out, SUB_2_out, MULT_2_out, DIV_2_out, AND_2_out, OR_3_out, xor_out);

  assign jr = ALU_op[4];
  assign slt = ALU_op[1];

  // Notes on the sheet:
  //   00100
  //   01100
  //   00101
  //   01101
  //   00110
  //   01110
  //   00111
  //   01111
  //   00001
  //   01001
  //   00010
  //   01010
  //   00011
  //   10000
  //   10001
  //   10010
  //   10011
  //   10100
  //   10101
  //   10110
  //   10111
  //   math
endmodule

// in/out
module Input___Output (
  input  [4:0] P_5,
  input  [4:0] P_4,
  input  [4:0] P_3,
  input  [31:0] Data_2,
  input  [4:0] P_2,
  input  [31:0] Data_1,
  input  Branch,
  input  R_type,
  output [31:0] input_to_ALU_2,
  output [31:0] input_to_ALU_1,
  output [4:0] \output ,
  output [4:0] input_1,
  output [4:0] input_2
);

  wire not_1_out, or_1_out;
  wire [31:0] bit_extender_1_out;

  assign bit_extender_1_out = {{22{1'b0}}, {P_4, P_5}};  // Bit_Extender bit_extender_1
  Multiplexer #(.width(5), .enable("false")) multiplexer_1 (.in0(P_4), .in1(P_2), .out(input_2), .sel(not_1_out));
  not not_1 (not_1_out, R_type);
  Multiplexer #(.width(32), .enable("false")) multiplexer_2 (
    .in0(bit_extender_1_out), .in1(Data_2), .out(input_to_ALU_2), .sel(or_1_out));
  or or_1 (or_1_out, Branch, R_type);

  assign input_1 = P_3;
  assign input_to_ALU_1 = Data_1;
  assign \output  = P_2;
endmodule

// GT
module greater_than (
  input  [31:0] input_1,
  input  [31:0] input_2,
  output \output 
);

  wire [31:0] subtractor_1_out;

  Subtractor #(.width(32)) subtractor_1 (.a(input_1), .b(input_2), .out(subtractor_1_out));  // open: bin, bout
  not not_1 (\output , subtractor_1_out[31]);
endmodule

module R_W (
  input  SW_prime,
  input  beq,
  input  bne,
  input  bqt,
  input  jr,
  output R_W
);

  wire not_1_out;

  not not_1 (not_1_out, SW_prime);
  or or_1 (R_W, not_1_out, beq, bne, bqt, jr);
endmodule
